# Fritzing sketch assignment_2 (saved by Fritzing 0.9.3b)
breadboards: 1

parts:
  元件3 = Arduino Uno (Rev3)
  LED9 = LED - 5mm [color="Green (565nm)" package="5 mm [THT]"]
  S12 = Pushbutton [package="[THT]"]
  R13 = Resistor [tolerance=±5% resistance=220 package=THT]
  元件6 = Ambient Light Sensor (TEMT6000 Breakout Board)
  hc-sr1 = hc-sr04
  元件7 = Max Power IR LED Kit
  R14 = Resistor [tolerance=±5% resistance=220 package=THT]
  R15 = Resistor [tolerance=±5% resistance=220 package=THT]
  R16 = Resistor [tolerance=±5% resistance=220 package=THT]
  LED15 = LED - 5mm [color="Green (565nm)" package="5 mm [THT]"]
  LED16 = LED - 5mm [color="Red (635nm)" package="5 mm [THT]"]
  Grove1 = Grove OLED 128x96
  J2 = Basic Servo
  R19 = Rotary Potentiometer (Small) [maximum_resistance=100kΩ package=THT]
  T2 = LM35 Temperature Sensor [package="TO92 [THT]"]

nets:
  N1: 元件3.A0, 元件6.S
  N2: 元件3.A1, T2.Vout
  N3: 元件3.A2, R19.wiper
  N4: 元件3.A4/SDA, Grove1.SDA
  N5: 元件3.A5/SCL, Grove1.SCL
  N6: 元件3.D8, hc-sr1.Echo
  N7: 元件3.D9_PWM, LED9.anode
  N8: 元件3.D10_PWM/SS, LED16.anode
  N9: 元件3.D13/SCK, LED15.anode
  N10: 元件3.D2, 元件7.CONTROL
  N11: 元件3.D3_PWM, J2.pulse
  N12: 元件3.D4, S12.Pin_3, S12.Pin_4, R13.Pin_1
  N13: 元件3.D7, hc-sr1.Trig
  VCC: 元件3.5V, S12.Pin_1, S12.Pin_2, 元件6.VCC, hc-sr1.VCC, 元件7.VCC, Grove1.VCC, J2.vcc, R19.leg1, T2.+Vs
  GND: 元件3.GND, R13.Pin_0, 元件6.GND, hc-sr1.GND, 元件7.GND, R14.Pin_0, R15.Pin_0, R16.Pin_0, Grove1.GND, J2.gnd, R19.leg2, T2.GND
  N14: LED9.cathode, R15.Pin_1
  N15: R14.Pin_1, LED16.cathode
  N16: R16.Pin_1, LED15.cathode
